# Fritzing sketch parking-lot (saved by Fritzing 0.9.10b)

parts:
  Part1 = Arduino Nano (Rev3.0)  # not connected
  Mod1 = Nano-V3-0-IO-Expansion-Adapter
  M3 = fc-51 [package=THT]
  M4 = fc-51 [package=THT]
  M5 = fc-51 [package=THT]
  M6 = fc-51 [package=THT]
  M7 = fc-51 [package=THT]
  U2 = LCD-16X2 [package=lcd-16x2]

nets:
  N1: Mod1.VCC, M3.pin3, M4.pin3, M5.pin3, M6.pin3, M7.pin3, U2.DB7
  N2: Mod1.GND, M3.pin2, M4.pin2, M5.pin2, M6.pin2, M7.pin2, U2.DB6
  N3: Mod1.D0/RX, U2.A
  N4: Mod1.D1/TX, U2.K
  N5: Mod1.D2, M3.pin1
  N6: Mod1.D4, M7.pin1
  N7: Mod1.D5_PWM, M6.pin1
  N8: Mod1.D7, M5.pin1
  N9: Mod1.D12/MISO, M4.pin1

notes:
  5 4 2
  RX, TX, 5V, GND
  12 7

custom parts:
  Nano-V3-0-IO-Expansion-Adapter: Nano V3.0 IO Expansion Adapter Shield. Note pcb view has been supressed as not useful. You can drag a Nano over the Nano connectors and it will connect and appear in schematic (although at present due to a bug, routing will not show as complete in breadboard).
